# Fritzing sketch Smart Coaster (saved by Fritzing 0.9.3b)
circuit board: 8.39349cm x 5.69298cm
breadboards: 1

parts:
  esp32 = Adafruit HUZZAH32 ESP32 Feather [part_number="Adafruit #3405"]
  part = Adafruit NeoPixel FeatherWing [part_number="Adafruit #2945"]
  R1 = Resistor [tolerance=±1% resistance=22k package=THT]
  J1 = Basic Force Sensing Resistor (FSR) [package=THT]

nets:
  N1: esp32.A2_I34, R1.Pin_1, J1.pin_1
  N2: esp32.GND, R1.Pin_0
  N3: esp32.3.3V, part.3V, J1.pin_0
  N4: esp32.VBAT, part.VBAT
  N5: esp32.VBUS, part.USB
  N6: esp32.IO32_A7, part.I

notes:
  SmartCoaster v0.1

custom parts:
  Adafruit NeoPixel FeatherWing: Put on your sunglasses before staring into these 32 configurable eye-blistering RGB LEDs. Arranged in a 4x8 matrix, each pixel is individually addressable. Only one pin is required to control all the LEDs. On the bottom we have jumpers for the DIN line to any of the I/O pins on a Feather. You can cut the default jumper trace and use any pin you like To make it easy to start, the LEDs are by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
